# Fritzing sketch esquema (saved by Fritzing 1.0.4)
breadboards: 1

parts:
  M1 = DOIT Esp32 DevKit v1 (30 pins long, 11 pins width) [part_number=ESP32S-PIN30]
  Componente1 = MQ-7 breakout
  R1 = Resistor [tolerance=±5% resistance=15k power=0.5W package="2512 [SMD]"]
  R2 = Resistor [tolerance=±5% resistance=10k power=0.5W package="2512 [SMD]"]

nets:
  GND: M1.GND, Componente1.GND, R1.Pin_1
  N1: M1.D32, R2.Pin_1
  VIN: M1.VIN, Componente1.VCC
  N2: Componente1.AO, R2.Pin_0

custom parts:
  DOIT Esp32 DevKit v1 (30 pins long, 11 pins width): The DOIT Esp32 DevKit v1 is one of the development board created by DOIT to evaluate the ESP-WROOM-32 module. It is based on the ESP32 microcontroller that boasts Wifi, Bluetooth, Ethernet and Low Power support all in a single chip. (vanepp) made breadboard work, adjusted pin numbering and labels and reduced size of schematic and cleaned up pcb. This chip is 30pins long (2 x15) and 11 pins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
  MQ-7 breakout: SKU: 101282
